// Logisim project 24BitMipsArchitecture.circ as structural Verilog: 6 circuits, main circuit main
module main (
  input  Reset,
  output [11:0] PC_ADDRESS,
  output [23:0] out_3,
  output [23:0] out_4
);

  wire alu_1_zerosignal, and_1_out, Clk_out, control_1_alu_0p1, control_1_alu_op_0, control_1_alu_src,
       control_1_branch, control_1_jump, control_1_mem_to_reg, control_1_mem_write, control_1_memread,
       control_1_regdst, control_1_regwrite;
  wire [3:0] alu_control_unit_1_out_4, multiplexer_3_out;
  wire [11:0] adder_1_out, adder_2_out, multiplexer_1_out, multiplexer_2_out;
  wire [23:0] alu_1_result, bit_extender_1_out, multiplexer_4_out, multiplexer_5_out, ram_1_data, rom_1_data;

  Clock Clk (.out(Clk_out));
  Register #(.width(12)) PC (.D(multiplexer_2_out), .Q(PC_ADDRESS), .clk(Clk_out), .clr(Reset));  // open: en
  Adder #(.width(12)) adder_1 (.a(PC_ADDRESS), .b(12'h1), .out(adder_1_out));  // open: cin, cout
  ROM #(.addrWidth(12), .dataWidth(24)) rom_1 (.addr(PC_ADDRESS), .data(rom_1_data));  // open: sel
  Adder #(.width(12)) adder_2 (.a(adder_1_out), .b(rom_1_data[11:0]), .out(adder_2_out));  // open: cin, cout
  Multiplexer #(.width(12)) multiplexer_1 (
    .in0(adder_1_out), .in1(adder_2_out), .out(multiplexer_1_out), .sel(and_1_out));  // open: en
  assign bit_extender_1_out = {{12{rom_1_data[11]}}, rom_1_data[11:0]};  // Bit_Extender bit_extender_1
  Control control_1 (
    .Input(rom_1_data[23:20]), .RegDst(control_1_regdst), .RegWrite(control_1_regwrite),
    .ALU_src(control_1_alu_src), .MEMread(control_1_memread), .Mem_write(control_1_mem_write),
    .Mem_to_reg(control_1_mem_to_reg), .alu_Op_0(control_1_alu_op_0), .alu_0p1(control_1_alu_0p1),
    .Branch(control_1_branch), .Jump(control_1_jump));
  Multiplexer #(.width(12)) multiplexer_2 (
    .in0(multiplexer_1_out), .in1(rom_1_data[11:0]), .out(multiplexer_2_out), .sel(control_1_jump));  // open: en
  Multiplexer #(.width(4)) multiplexer_3 (
    .in0(rom_1_data[15:12]), .in1(rom_1_data[11:8]), .out(multiplexer_3_out), .sel(control_1_regdst));  // open: en
  and and_1 (and_1_out, alu_1_zerosignal, control_1_alu_op_0);
  RegisterFile registerfile_1 (
    .RS(rom_1_data[19:16]), .RT(rom_1_data[15:12]), .Data_In(multiplexer_5_out), .RD(multiplexer_3_out),
    .REGWRITE(control_1_regwrite), .OUT1(out_3), .OUT2(out_4), .CLK(Clk_out));
  ALU_Control_Unit alu_control_unit_1 (
    .ALUOp0(control_1_branch), .ALUOp1(control_1_alu_0p1), .Function(rom_1_data[3:0]),
    .out_4(alu_control_unit_1_out_4));
  Multiplexer #(.width(24)) multiplexer_4 (
    .in0(out_4), .in1(bit_extender_1_out), .out(multiplexer_4_out), .sel(control_1_alu_src));  // open: en
  ALU alu_1 (
    .Bin(alu_control_unit_1_out_4[3]), .func(alu_control_unit_1_out_4[2:0]), .A(out_3),
    .result(alu_1_result), .ZeroSignal(alu_1_zerosignal), .Cin(1'b0), .B(multiplexer_4_out));  // open: Overflow, Cout
  RAM #(.addrWidth(24), .dataWidth(24), .bus("separate")) ram_1 (
    .addr(alu_1_result), .din(out_4), .data(ram_1_data), .str(control_1_mem_write), .clk(Clk_out),
    .ld(control_1_memread));  // open: sel, clr
  Multiplexer #(.width(24)) multiplexer_5 (
    .in0(alu_1_result), .in1(ram_1_data), .out(multiplexer_5_out), .sel(control_1_mem_to_reg));  // open: en

  // Notes on the sheet:
  //   ALU Operations
  //   ADD -> 0000
  //   SUB, AND, OR, NAND, NOR
  //   contents of rom_1 (hex, n*v repeats v):
  //   356004 101001 102002 12300 203003 0 400000
  //   JUMP
  //   Branch and ZERO
endmodule

module RegisterFile (
  input  [3:0] RS,
  input  [3:0] RT,
  input  [23:0] Data_In,
  input  [3:0] RD,
  input  CLK,
  input  REGWRITE,
  output [23:0] OUT1,
  output [23:0] OUT2
);

  wire and_1_out, decoder_1_out0, decoder_1_out1, decoder_1_out2, decoder_1_out3, decoder_1_out4,
       decoder_1_out5, decoder_1_out6, decoder_1_out7, decoder_1_out8, decoder_1_out9, decoder_1_out10,
       decoder_1_out11, decoder_1_out12, decoder_1_out13, decoder_1_out14, decoder_1_out15;
  wire [23:0] register_1_q, register_2_q, register_3_q, register_4_q, register_5_q, register_6_q,
       register_7_q, register_8_q, register_9_q, register_10_q, register_11_q, register_12_q, register_13_q,
       register_14_q, register_15_q, register_16_q;

  Decoder #(.select(4)) decoder_1 (
    .out0(decoder_1_out0), .out1(decoder_1_out1), .out2(decoder_1_out2), .out3(decoder_1_out3),
    .out4(decoder_1_out4), .out5(decoder_1_out5), .out6(decoder_1_out6), .out7(decoder_1_out7),
    .out8(decoder_1_out8), .out9(decoder_1_out9), .out10(decoder_1_out10), .out11(decoder_1_out11),
    .out12(decoder_1_out12), .out13(decoder_1_out13), .out14(decoder_1_out14), .out15(decoder_1_out15),
    .sel(RD));  // open: en
  and and_1 (and_1_out, CLK, REGWRITE);
  Register #(.width(24)) register_1 (.D(Data_In), .en(decoder_1_out0), .Q(register_1_q), .clk(and_1_out));  // open: clr
  Register #(.width(24)) register_2 (.D(Data_In), .en(decoder_1_out1), .Q(register_2_q), .clk(and_1_out));  // open: clr
  Register #(.width(24)) register_3 (.D(Data_In), .en(decoder_1_out2), .Q(register_3_q), .clk(and_1_out));  // open: clr
  Register #(.width(24)) register_4 (.D(Data_In), .en(decoder_1_out3), .Q(register_4_q), .clk(and_1_out));  // open: clr
  Register #(.width(24)) register_5 (.D(Data_In), .en(decoder_1_out4), .Q(register_5_q), .clk(and_1_out));  // open: clr
  Register #(.width(24)) register_6 (.D(Data_In), .en(decoder_1_out5), .Q(register_6_q), .clk(and_1_out));  // open: clr
  Register #(.width(24)) register_7 (.D(Data_In), .en(decoder_1_out6), .Q(register_7_q), .clk(and_1_out));  // open: clr
  Register #(.width(24)) register_8 (.D(Data_In), .en(decoder_1_out7), .Q(register_8_q), .clk(and_1_out));  // open: clr
  Register #(.width(24)) register_9 (.D(Data_In), .en(decoder_1_out8), .Q(register_9_q), .clk(and_1_out));  // open: clr
  Register #(.width(24)) register_10 (
    .D(Data_In), .en(decoder_1_out9), .Q(register_10_q), .clk(and_1_out));  // open: clr
  Register #(.width(24)) register_11 (
    .D(Data_In), .en(decoder_1_out10), .Q(register_11_q), .clk(and_1_out));  // open: clr
  Register #(.width(24)) register_12 (
    .D(Data_In), .en(decoder_1_out11), .Q(register_12_q), .clk(and_1_out));  // open: clr
  Register #(.width(24)) register_13 (
    .D(Data_In), .en(decoder_1_out12), .Q(register_13_q), .clk(and_1_out));  // open: clr
  Register #(.width(24)) register_14 (
    .D(Data_In), .en(decoder_1_out13), .Q(register_14_q), .clk(and_1_out));  // open: clr
  Register #(.width(24)) register_15 (
    .D(Data_In), .en(decoder_1_out14), .Q(register_15_q), .clk(and_1_out));  // open: clr
  Register #(.width(24)) register_16 (
    .D(Data_In), .en(decoder_1_out15), .Q(register_16_q), .clk(and_1_out));  // open: clr
  Multiplexer #(.select(4), .width(24)) multiplexer_1 (
    .in0(register_1_q), .in1(register_2_q), .in2(register_3_q), .in3(register_4_q), .in4(register_5_q),
    .in5(register_6_q), .in6(register_7_q), .in7(register_8_q), .in8(register_9_q), .in9(register_10_q),
    .in10(register_11_q), .in11(register_12_q), .in12(register_13_q), .in13(register_14_q),
    .in14(register_15_q), .in15(register_16_q), .out(OUT1), .sel(RS));  // open: en
  Multiplexer #(.select(4), .width(24)) multiplexer_2 (
    .in0(register_1_q), .in1(register_2_q), .in2(register_3_q), .in3(register_4_q), .in4(register_5_q),
    .in5(register_6_q), .in6(register_7_q), .in7(register_8_q), .in8(register_9_q), .in9(register_10_q),
    .in10(register_11_q), .in11(register_12_q), .in12(register_13_q), .in13(register_14_q),
    .in14(register_15_q), .in15(register_16_q), .out(OUT2), .sel(RT));  // open: en
endmodule

module ALU (
  input  [23:0] A,
  input  Bin,
  input  [2:0] func,
  input  [23:0] B,
  input  Cin,
  output [23:0] result,
  output ZeroSignal,
  output Overflow,
  output Cout
);

  wire alu_1_bit_1_cout, alu_1_bit_2_cout, alu_1_bit_3_cout, alu_1_bit_4_cout, alu_1_bit_5_cout,
       alu_1_bit_6_cout, alu_1_bit_7_cout, alu_1_bit_8_cout, alu_1_bit_9_cout, alu_1_bit_10_cout,
       alu_1_bit_11_cout, alu_1_bit_12_cout, alu_1_bit_13_cout, alu_1_bit_14_cout, alu_1_bit_15_cout,
       alu_1_bit_16_cout, alu_1_bit_17_cout, alu_1_bit_18_cout, alu_1_bit_19_cout, alu_1_bit_20_cout,
       alu_1_bit_21_cout, alu_1_bit_22_cout, alu_1_bit_23_cout;
  wire [23:0] adder_1_out, alu_1_bit_1_res;

  ALU_1_Bit alu_1_bit_1 (
    .Cin(Cin), .A(A[0]), .B(B[0]), .Opselect(func), .bin(Bin), .res(alu_1_bit_1_res[0]),
    .Cout(alu_1_bit_1_cout));
  ALU_1_Bit alu_1_bit_2 (
    .Cin(alu_1_bit_1_cout), .A(A[1]), .B(B[1]), .Opselect(func), .bin(Bin), .res(alu_1_bit_1_res[1]),
    .Cout(alu_1_bit_2_cout));
  ALU_1_Bit alu_1_bit_3 (
    .Cin(alu_1_bit_2_cout), .A(A[2]), .B(B[2]), .Opselect(func), .bin(Bin), .res(alu_1_bit_1_res[2]),
    .Cout(alu_1_bit_3_cout));
  ALU_1_Bit alu_1_bit_4 (
    .Cin(alu_1_bit_3_cout), .A(A[3]), .B(B[3]), .Opselect(func), .bin(Bin), .res(alu_1_bit_1_res[3]),
    .Cout(alu_1_bit_4_cout));
  ALU_1_Bit alu_1_bit_5 (
    .Cin(alu_1_bit_4_cout), .A(A[4]), .B(B[4]), .Opselect(func), .bin(Bin), .res(alu_1_bit_1_res[4]),
    .Cout(alu_1_bit_5_cout));
  ALU_1_Bit alu_1_bit_6 (
    .Cin(alu_1_bit_5_cout), .A(A[5]), .B(B[5]), .Opselect(func), .bin(Bin), .res(alu_1_bit_1_res[5]),
    .Cout(alu_1_bit_6_cout));
  ALU_1_Bit alu_1_bit_7 (
    .Cin(alu_1_bit_6_cout), .A(A[6]), .B(B[6]), .Opselect(func), .bin(Bin), .res(alu_1_bit_1_res[6]),
    .Cout(alu_1_bit_7_cout));
  ALU_1_Bit alu_1_bit_8 (
    .Cin(alu_1_bit_7_cout), .A(A[7]), .B(B[7]), .Opselect(func), .bin(Bin), .res(alu_1_bit_1_res[7]),
    .Cout(alu_1_bit_8_cout));
  ALU_1_Bit alu_1_bit_9 (
    .Cin(alu_1_bit_8_cout), .A(A[8]), .B(B[8]), .Opselect(func), .bin(Bin), .res(alu_1_bit_1_res[8]),
    .Cout(alu_1_bit_9_cout));
  ALU_1_Bit alu_1_bit_10 (
    .Cin(alu_1_bit_9_cout), .A(A[9]), .B(B[9]), .Opselect(func), .bin(Bin), .res(alu_1_bit_1_res[9]),
    .Cout(alu_1_bit_10_cout));
  ALU_1_Bit alu_1_bit_11 (
    .Cin(alu_1_bit_10_cout), .A(A[10]), .B(B[10]), .Opselect(func), .bin(Bin), .res(alu_1_bit_1_res[10]),
    .Cout(alu_1_bit_11_cout));
  ALU_1_Bit alu_1_bit_12 (
    .Cin(alu_1_bit_11_cout), .A(A[11]), .B(B[11]), .Opselect(func), .bin(Bin), .res(alu_1_bit_1_res[11]),
    .Cout(alu_1_bit_12_cout));
  ALU_1_Bit alu_1_bit_13 (
    .Cin(alu_1_bit_12_cout), .A(A[12]), .B(B[12]), .Opselect(func), .bin(Bin), .res(alu_1_bit_1_res[12]),
    .Cout(alu_1_bit_13_cout));
  ALU_1_Bit alu_1_bit_14 (
    .Cin(alu_1_bit_13_cout), .A(A[13]), .B(B[13]), .Opselect(func), .bin(Bin), .res(alu_1_bit_1_res[13]),
    .Cout(alu_1_bit_14_cout));
  ALU_1_Bit alu_1_bit_15 (
    .Cin(alu_1_bit_14_cout), .A(A[14]), .B(B[14]), .Opselect(func), .bin(Bin), .res(alu_1_bit_1_res[14]),
    .Cout(alu_1_bit_15_cout));
  ALU_1_Bit alu_1_bit_16 (
    .Cin(alu_1_bit_15_cout), .A(A[15]), .B(B[15]), .Opselect(func), .bin(Bin), .res(alu_1_bit_1_res[15]),
    .Cout(alu_1_bit_16_cout));
  ALU_1_Bit alu_1_bit_17 (
    .Cin(alu_1_bit_16_cout), .A(A[16]), .B(B[16]), .Opselect(func), .bin(Bin), .res(alu_1_bit_1_res[16]),
    .Cout(alu_1_bit_17_cout));
  ALU_1_Bit alu_1_bit_18 (
    .Cin(alu_1_bit_17_cout), .A(A[17]), .B(B[17]), .Opselect(func), .bin(Bin), .res(alu_1_bit_1_res[17]),
    .Cout(alu_1_bit_18_cout));
  ALU_1_Bit alu_1_bit_19 (
    .Cin(alu_1_bit_18_cout), .A(A[18]), .B(B[18]), .Opselect(func), .bin(Bin), .res(alu_1_bit_1_res[18]),
    .Cout(alu_1_bit_19_cout));
  ALU_1_Bit alu_1_bit_20 (
    .Cin(alu_1_bit_19_cout), .A(A[19]), .B(B[19]), .Opselect(func), .bin(Bin), .res(alu_1_bit_1_res[19]),
    .Cout(alu_1_bit_20_cout));
  ALU_1_Bit alu_1_bit_21 (
    .Cin(alu_1_bit_20_cout), .A(A[20]), .B(B[20]), .Opselect(func), .bin(Bin), .res(alu_1_bit_1_res[20]),
    .Cout(alu_1_bit_21_cout));
  ALU_1_Bit alu_1_bit_22 (
    .Cin(alu_1_bit_21_cout), .A(A[21]), .B(B[21]), .Opselect(func), .bin(Bin), .res(alu_1_bit_1_res[21]),
    .Cout(alu_1_bit_22_cout));
  ALU_1_Bit alu_1_bit_23 (
    .Cin(alu_1_bit_22_cout), .A(A[22]), .B(B[22]), .Opselect(func), .bin(Bin), .res(alu_1_bit_1_res[22]),
    .Cout(alu_1_bit_23_cout));
  ALU_1_Bit alu_1_bit_24 (
    .Cin(alu_1_bit_23_cout), .A(A[23]), .B(B[23]), .Opselect(func), .bin(Bin), .res(alu_1_bit_1_res[23]),
    .Cout(Cout));
  xor xor_1 (Overflow, alu_1_bit_23_cout, Cout);
  nor nor_1 (ZeroSignal, result[0], result[1], result[2], result[3], result[4], result[5], result[6], result[7], result[8], result[9], result[10], result[11], result[12], result[13], result[14], result[15], result[16], result[17], result[18], result[19], result[20], result[21], result[22], result[23]);
  Adder #(.width(24)) adder_1 (.a(24'h1), .b(alu_1_bit_1_res), .out(adder_1_out));  // open: cin, cout
  Multiplexer #(.width(24)) multiplexer_1 (
    .in0(alu_1_bit_1_res), .in1(adder_1_out), .out(result), .sel(Bin));  // open: en
endmodule

module Control (
  input  [3:0] Input,
  output RegDst,
  output RegWrite,
  output ALU_src,
  output MEMread,
  output Mem_write,
  output Mem_to_reg,
  output alu_Op_0,
  output alu_0p1,
  output Branch,
  output Jump
);

  nor nor_1 (alu_0p1, Input[0], Input[1], Input[2], Input[3]);
  and and_1 (Mem_to_reg, Input[0], ~Input[1], ~Input[2], ~Input[3]);  // AND_Gate
  and and_2 (Mem_write, ~Input[0], Input[1], ~Input[2], ~Input[3]);  // AND_Gate
  and and_3 (alu_Op_0, Input[0], Input[1], ~Input[2], ~Input[3]);  // AND_Gate
  and and_4 (Jump, ~Input[0], ~Input[1], Input[2], ~Input[3]);  // AND_Gate
  or or_1 (RegWrite, alu_0p1, Mem_to_reg);
  or or_2 (ALU_src, Mem_to_reg, Mem_write);

  assign Branch = alu_Op_0;
  assign MEMread = Mem_to_reg;
  assign RegDst = alu_0p1;

  // Notes on the sheet:
  //   LW
  //   R-type
  //   SW
  //   BEQ
  //   JUMP
endmodule

module ALU_Control_Unit (
  input  ALUOp0,
  input  ALUOp1,
  input  [3:0] Function,
  output [3:0] out_4
);

  wire LW_SW_out, not_1_out, not_2_out, R___ADD_out, R___AND_out, R___NAND_out, R___NOR_out, R___OR_out,
       R___SUB_out;

  not not_1 (not_1_out, ALUOp0);
  not not_2 (not_2_out, ALUOp1);
  and LW_SW (LW_SW_out, not_1_out, not_2_out);
  and R___ADD (R___ADD_out, ALUOp1, ~Function[0], ~Function[1], ~Function[2], ~Function[3]);  // AND_Gate
  and R___SUB (R___SUB_out, ALUOp1, Function[0], ~Function[1], ~Function[2], ~Function[3]);  // AND_Gate
  and R___AND (R___AND_out, ALUOp1, ~Function[0], Function[1], ~Function[2], ~Function[3]);  // AND_Gate
  and R___OR (R___OR_out, ALUOp1, Function[0], Function[1], ~Function[2], ~Function[3]);  // AND_Gate
  and R___NAND (R___NAND_out, ALUOp1, ~Function[0], ~Function[1], Function[2], ~Function[3]);  // AND_Gate
  and R___NOR (R___NOR_out, ALUOp1, Function[0], ~Function[1], Function[2], ~Function[3]);  // AND_Gate
  or or_1 (out_4[3], ALUOp0, R___SUB_out);
  or or_2 (out_4[2], LW_SW_out, ALUOp0, R___ADD_out, R___SUB_out);
  or or_3 (out_4[1], R___NOR_out, R___NAND_out);
  or or_4 (out_4[0], R___OR_out, R___NAND_out);

  // Notes on the sheet:
  //   BRANCH
endmodule

module ALU_1_Bit (
  input  Cin,
  input  A,
  input  B,
  input  [2:0] Opselect,
  input  bin,
  output res,
  output Cout
);

  wire adder_1_out, and_1_out, multiplexer_1_out, nand_1_out, nor_1_out, not_1_out, or_1_out, xor_1_out;

  not not_1 (not_1_out, B);
  Multiplexer multiplexer_1 (.in0(B), .in1(not_1_out), .out(multiplexer_1_out), .sel(bin));  // open: en
  and and_1 (and_1_out, A, B);
  or or_1 (or_1_out, A, B);
  nor nor_1 (nor_1_out, A, B);
  nand nand_1 (nand_1_out, A, B);
  Adder #(.width(1)) adder_1 (.a(A), .b(multiplexer_1_out), .out(adder_1_out), .cin(Cin), .cout(Cout));
  xor xor_1 (xor_1_out, A, B);
  Multiplexer #(.select(3)) multiplexer_2 (
    .in0(and_1_out), .in1(or_1_out), .in2(nor_1_out), .in3(nand_1_out), .in4(adder_1_out), .in5(xor_1_out),
    .out(res), .sel(Opselect));  // open: in6, in7, en
endmodule
