// Logisim project ALUDesign16Bits.circ as structural Verilog: 3 circuits, main circuit main
module main (
  input  [2:0] Operation,
  input  Cin,
  input  [15:0] A,
  input  [15:0] B,
  output [15:0] out_5,
  output Zero_Flag,
  output OverFlow,
  output COut
);

  ALU16Bit alu16bit_1 (
    .BInput(Operation[2]), .Cin(Cin), .Operation(Operation[1:0]), .A(A), .B(B), .Output(out_5),
    .out_7(Zero_Flag), .Overflow_Flag(OverFlow), .COut(COut));
endmodule

module ALU (
  input  Cin,
  input  A,
  input  B,
  input  Binput,
  input  [1:0] Operation,
  output Output,
  output Cout
);

  wire adder_1_out, and_1_out, multiplexer_1_out, not_1_out, not_2_out, or_1_out;

  Multiplexer multiplexer_1 (.in0(B), .in1(not_1_out), .out(multiplexer_1_out), .sel(Binput));  // open: en
  not not_1 (not_1_out, B);
  and and_1 (and_1_out, A, B);
  or or_1 (or_1_out, A, B);
  not not_2 (not_2_out, A);
  Adder #(.width(1)) adder_1 (.a(A), .b(multiplexer_1_out), .out(adder_1_out), .cin(Cin), .cout(Cout));
  Multiplexer #(.select(2)) multiplexer_2 (
    .in0(and_1_out), .in1(or_1_out), .in2(adder_1_out), .in3(not_2_out), .out(Output), .sel(Operation));  // open: en
endmodule

// ALU16BIT
module ALU16Bit (
  input  BInput,
  input  Cin,
  input  [1:0] Operation,
  input  [15:0] A,
  input  [15:0] B,
  output [15:0] Output,
  output out_7,
  output Overflow_Flag,
  output COut
);

  wire alu_1_cout, alu_2_cout, alu_3_cout, alu_4_cout, alu_5_cout, alu_6_cout, alu_7_cout, alu_8_cout,
       alu_9_cout, alu_10_cout, alu_11_cout, alu_12_cout, alu_13_cout, alu_14_cout, alu_15_cout;

  ALU alu_1 (
    .Cin(Cin), .A(A[0]), .B(B[0]), .Binput(BInput), .Operation(Operation), .Output(Output[0]),
    .Cout(alu_1_cout));
  ALU alu_2 (
    .Cin(alu_1_cout), .A(A[1]), .B(B[1]), .Binput(BInput), .Operation(Operation), .Output(Output[1]),
    .Cout(alu_2_cout));
  ALU alu_3 (
    .Cin(alu_2_cout), .A(A[2]), .B(B[2]), .Binput(BInput), .Operation(Operation), .Output(Output[2]),
    .Cout(alu_3_cout));
  ALU alu_4 (
    .Cin(alu_3_cout), .A(A[3]), .B(B[3]), .Binput(BInput), .Operation(Operation), .Output(Output[3]),
    .Cout(alu_4_cout));
  ALU alu_5 (
    .Cin(alu_4_cout), .A(A[4]), .B(B[4]), .Binput(BInput), .Operation(Operation), .Output(Output[4]),
    .Cout(alu_5_cout));
  ALU alu_6 (
    .Cin(alu_5_cout), .A(A[5]), .B(B[5]), .Binput(BInput), .Operation(Operation), .Output(Output[5]),
    .Cout(alu_6_cout));
  ALU alu_7 (
    .Cin(alu_6_cout), .A(A[6]), .B(B[6]), .Binput(BInput), .Operation(Operation), .Output(Output[6]),
    .Cout(alu_7_cout));
  ALU alu_8 (
    .Cin(alu_7_cout), .A(A[7]), .B(B[7]), .Binput(BInput), .Operation(Operation), .Output(Output[7]),
    .Cout(alu_8_cout));
  ALU alu_9 (
    .Cin(alu_8_cout), .A(A[8]), .B(B[8]), .Binput(BInput), .Operation(Operation), .Output(Output[8]),
    .Cout(alu_9_cout));
  ALU alu_10 (
    .Cin(alu_9_cout), .A(A[9]), .B(B[9]), .Binput(BInput), .Operation(Operation), .Output(Output[9]),
    .Cout(alu_10_cout));
  ALU alu_11 (
    .Cin(alu_10_cout), .A(A[10]), .B(B[10]), .Binput(BInput), .Operation(Operation), .Output(Output[10]),
    .Cout(alu_11_cout));
  ALU alu_12 (
    .Cin(alu_11_cout), .A(A[11]), .B(B[11]), .Binput(BInput), .Operation(Operation), .Output(Output[11]),
    .Cout(alu_12_cout));
  ALU alu_13 (
    .Cin(alu_12_cout), .A(A[12]), .B(B[12]), .Binput(BInput), .Operation(Operation), .Output(Output[12]),
    .Cout(alu_13_cout));
  ALU alu_14 (
    .Cin(alu_13_cout), .A(A[13]), .B(B[13]), .Binput(BInput), .Operation(Operation), .Output(Output[13]),
    .Cout(alu_14_cout));
  ALU alu_15 (
    .Cin(alu_14_cout), .A(A[14]), .B(B[14]), .Binput(BInput), .Operation(Operation), .Output(Output[14]),
    .Cout(alu_15_cout));
  ALU alu_16 (
    .Cin(alu_15_cout), .A(A[15]), .B(B[15]), .Binput(BInput), .Operation(Operation), .Output(Output[15]),
    .Cout(COut));
  nor nor_1 (out_7, Output[0], Output[1], Output[2], Output[3], Output[4], Output[5], Output[6], Output[7], Output[8], Output[9], Output[10], Output[11], Output[12], Output[13], Output[14], Output[15]);
  xor xor_1 (Overflow_Flag, alu_15_cout, COut);
endmodule
