// Logisim project ControlUnit.circ as structural Verilog: 1 circuit, main circuit main
module main (
  input  [3:0] OPCODE,
  input  in_2,
  output RegDst,
  output ALUSrc,
  output MemToReg,
  output RegWrite,
  output MemRead,
  output MemWrite,
  output [1:0] ALUOp
);

  and R_Type (ALUOp[0], ~OPCODE[0], ~OPCODE[1], ~OPCODE[2], ~OPCODE[3]);  // AND_Gate
  and LW (MemRead, OPCODE[0], OPCODE[1], ~OPCODE[2], ~OPCODE[3]);  // AND_Gate
  and SW (MemWrite, OPCODE[0], OPCODE[1], ~OPCODE[2], OPCODE[3]);  // AND_Gate
  or or_1 (ALUSrc, MemRead, MemWrite);
  or or_2 (RegWrite, MemRead, ALUOp[0]);

  assign ALUOp[1] = in_2;
  assign MemToReg = MemRead;
  assign RegDst = ALUOp[0];
endmodule
